# Fritzing sketch Slipring Sword (saved by Fritzing 0.9.4)

parts:
  MP3-1 = Serial MP3 Player
  Part1 = Arduino Nano (Rev3.0)
  NEOPIXEL1 = Neopixel Strip -- White (60/m) [part_number=1138]  # not connected
  R1 = Resistor [tolerance=±5% resistance=330 package=THT]  # not connected
  S1 = Reed switch [package=THT]
  S2 = Reed switch [package=THT]
  S3 = Reed switch [package=THT]
  S4 = Reed switch [package=THT]
  S5 = Reed switch [package=THT]
  S6 = Reed switch [package=THT]
  JACK1 = 2.1mm Barrel Jack with Terminal Block
  C2 = Electrolytic Capacitor [capacitance=0.1µF package="100 mil [THT, electrolytic]"]

nets:
  N1: MP3-1.pin1, Part1.GND, S1.pin_2, S2.pin_2, S3.pin_2, S4.pin_2, S5.pin_2, S6.pin_2, JACK1.NEG, C2.-
  N2: MP3-1.pin2, JACK1.POS, C2.+
  N3: MP3-1.pin3, Part1.D8
  N4: MP3-1.pin4, Part1.D9
  N5: Part1.D2, S6.pin_1
  N6: Part1.D3, S5.pin_1
  N7: Part1.D4, S4.pin_1
  N8: Part1.D5, S3.pin_1
  N9: Part1.D6, S2.pin_1
  N10: Part1.D7, S1.pin_1

notes:
  WS2812B programmable LED strip
  5V, GND, and DataIn connected via 330Ω series resistor to Arduino GPIO pin A5
  5V DC Power Supply, with 6.3V 1000µF capacitor across + and - terminals
  RC35 Magnet sensors connected between Arduino pins D2-D7 and GND
  YX5200 Serial MP3 Player
  5V - 5V
  GND - GND
  Tx - Arduino Pin 9
  Rx - Arduino Pin 8

custom parts:
  Serial MP3 Player: The module is a kind of simple MP3 player device which is based on a high-quality MP3 audio chip---YX5300. It can support 8k Hz ~ 48k Hz sampling frequency MP3 and WAV file formats. There is a TF card socket on board, so you can plug the micro SD card that stores audio files. MCU can control the MP3 playback state by sending commands to the module via UART port, such as switch songs, change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
  Neopixel Strip -- White (60/m): Neopixel Strip, White, 60 pixels per meter.
